# Fritzing sketch ArduinoBoard (saved by Fritzing 0.7.12b)
breadboards: 1

parts:
  Arduino = Arduino
  Αισθητήρας_Θερμοκρασίας/Υγρασίας = Humidity Sensor - HIH-4030 Breakout [part_number=XXX-HT]
  Γυροσκόπιο_Αξελερόμετρο = Tri-Axis Gyro Breakout - L3G4200D [part_number=XXX-GA]
  Τροφοδοσία_Ασύρματου_Module = Battery block 9V [part_number=XXX-VCC]
  Radio_Tranceiver = nRF24L01 2.4Ghz Tranceiver [part_number=XXX-NRF]
  R3 = Resistor [tolerance=±5% resistance=4k package=THT]

nets (from the breadboard view):
  GND: Arduino.GND, Αισθητήρας_Θερμοκρασίας/Υγρασίας.GND, Γυροσκόπιο_Αξελερόμετρο.GND, Τροφοδοσία_Ασύρματου_Module.-, Radio_Tranceiver.GND
  N1: Arduino.D13, Radio_Tranceiver.CE
  N2: Arduino.D12, Radio_Tranceiver.SCK
  N3: Arduino.D11, Radio_Tranceiver.MI
  N4: Arduino.D10, Radio_Tranceiver.CSN
  N5: Arduino.D9, Radio_Tranceiver.MO
  N6: Arduino.D8, Radio_Tranceiver.IRQ
  N7: Arduino.D7, Γυροσκόπιο_Αξελερόμετρο.SDO
  N8: Arduino.D6, Γυροσκόπιο_Αξελερόμετρο.CS
  N9: Arduino.D5, Γυροσκόπιο_Αξελερόμετρο.INT2
  N10: Arduino.D4, Γυροσκόπιο_Αξελερόμετρο.INT1
  N11: Arduino.D2, Αισθητήρας_Θερμοκρασίας/Υγρασίας.OUT
  VCC: Arduino.3V3, Γυροσκόπιο_Αξελερόμετρο.VCC, Radio_Tranceiver.VCC, R3.Pin_0
  +5V: Arduino.+5V, Αισθητήρας_Θερμοκρασίας/Υγρασίας.VCC
  N12: Arduino.VIN, Τροφοδοσία_Ασύρματου_Module.+
  N13: Γυροσκόπιο_Αξελερόμετρο.SCL, Γυροσκόπιο_Αξελερόμετρο.SDA, R3.Pin_1
