# Fritzing sketch ArduinoMainBoard (saved by Fritzing 0.7.12b)
breadboards: 1

parts:
  Arduino = Arduino
  Radio_Tranceiver = nRF24L01 2.4Ghz Tranceiver [part_number=XXX-NRF]

nets:
  GND: Arduino.GND, Radio_Tranceiver.GND
  N1: Arduino.D13, Radio_Tranceiver.CE
  N2: Arduino.D12, Radio_Tranceiver.SCK
  N3: Arduino.D11, Radio_Tranceiver.MI
  N4: Arduino.D10, Radio_Tranceiver.CSN
  N5: Arduino.D9, Radio_Tranceiver.MO
  N6: Arduino.D8, Radio_Tranceiver.IRQ
  3V3: Arduino.3V3, Radio_Tranceiver.VCC
